# Fritzing sketch miniturtlebot (saved by Fritzing 0.9.6b)
breadboards: 4

parts:
  U1 = LuaNode32 / ESP32 [part_number=ESP32S-PIN30]
  J1_Left_Servo = Dagu DGServo 9g header (male) [package=THT]
  J2_Right_Servo = Dagu DGServo 9g header (male) [package=THT]
  HC-SR04_Sensor_1 = HC-SR04 Ultrasonic Distance Sensor
  HC-SR04_Sensor_2 = HC-SR04 Ultrasonic Distance Sensor
  R1 = Resistor [tolerance=±5% power=0.25 resistance=1.8k package=THT]
  R2 = Resistor [tolerance=±5% power=0.25 resistance=3.3k package=THT]
  R3 = Resistor [tolerance=±5% power=0.25 resistance=1.8k package=THT]
  R4 = Resistor [tolerance=±5% power=0.25 resistance=3.3k package=THT]

nets:
  GND: U1.GND, J1_Left_Servo.gnd, J2_Right_Servo.gnd, HC-SR04_Sensor_1.GND, HC-SR04_Sensor_2.GND, R2.Pin_0, R4.Pin_0
  5V: U1.Vin, J1_Left_Servo.Vcc, J2_Right_Servo.Vcc, HC-SR04_Sensor_1.VCC, HC-SR04_Sensor_2.VCC
  3.3V: U1.3V3
  N1: U1.D2, HC-SR04_Sensor_2.TRIG
  N2: U1.D4, R3.Pin_1, R4.Pin_1
  N3: U1.D18, HC-SR04_Sensor_1.TRIG
  N4: U1.D19, R1.Pin_1, R2.Pin_1
  N5: U1.D22, J2_Right_Servo.pulse
  N6: U1.D23, J1_Left_Servo.pulse
  N7: HC-SR04_Sensor_1.ECHO, R1.Pin_0
  N8: HC-SR04_Sensor_2.ECHO, R3.Pin_0

custom parts:
  LuaNode32 / ESP32: New Image for LuaNode32 DOIT ESP32 DEVKIT V1. Base parts from LuaNode32 / ESP32 ESP32 based LuaNode32 by G.Noorlander DOIT Esp32 DevKit v1 (30 pins long, 11 pins width) by Werner Rothschopf (modified by vanepp Dec 2018)
