# Fritzing sketch test_breadboard (saved by Fritzing 0.9.6b)
breadboards: 2

parts:
  U1 = LuaNode32 / ESP32 [part_number=ESP32S-PIN30]
  J1 = Dagu DGServo 9g header (male) [package=THT]
  J2 = Dagu DGServo 9g header (male) [package=THT]

nets:
  N1: U1.D32, J1.pulse
  N2: U1.D33, J2.pulse
  GND: U1.GND, J1.gnd, J2.gnd
  VCC: U1.Vin, J1.Vcc, J2.Vcc

custom parts:
  LuaNode32 / ESP32: New Image for LuaNode32 DOIT ESP32 DEVKIT V1. Base parts from LuaNode32 / ESP32 ESP32 based LuaNode32 by G.Noorlander DOIT Esp32 DevKit v1 (30 pins long, 11 pins width) by Werner Rothschopf (modified by vanepp Dec 2018)
